// Logisim project 908857_zubenko_andrea_ae1lab_circuito.circ as structural Verilog: 9 circuits, main circuit main
module main (
  output out_1,
  output out_2
);

  wire and_1_out, Box1Err, Box2Err, Box3Err, Box4Err, Box5Err, Box6Err, Box7Err, Box8Err, Box9Err, BoxErr,
       Col1Err, Col2Err, Col3Err, Col4Err, Col5Err, Col6Err, Col7Err, Col8Err, Col9Err, ColErr, Riga1Err,
       Riga1Somma, Riga2Err, Riga2Somma, Riga3Err, Riga3Somma, Riga4Err, Riga4Somma, Riga5Err, Riga5Somma,
       Riga6Err, Riga6Somma, Riga7Err, Riga7Somma, Riga8Err, Riga8Somma, Riga9Err, Riga9Somma, RigaErr;
  wire [3:0] N1, N2, N3, N4, N5, N6, N7, N8, N9, N10, N11, N12, N13, N14, N15, N16, N17, N18, N19, N20, N21,
       N22, N23, N24, N25, N26, N27, N28, N29, N30, N31, N32, N33, N34, N35, N36, N37, N38, N39, N40, N41,
       N42, N43, N44, N45, N46, N47, N48, N49, N50, N51, N52, N53, N54, N55, N56, N57, N58, N59, N60, N61,
       N62, N63, N64, N65, N66, N67, N68, N69, N70, N71, N72, N73, N74, N75, N76, N77, N78, N79, N80, N81;

  // Big_Hex_Digit_Display big_hex_digit_display_1: pin names not known
  // Sudoku_Counter sudoku_counter_1: pin names not known
  // Sudoku_Counter sudoku_counter_2: pin names not known; wires that end beside it: N1
  // Big_Hex_Digit_Display big_hex_digit_display_2: pin names not known
  // Big_Hex_Digit_Display big_hex_digit_display_3: pin names not known; wires that end beside it: N10
  // Sudoku_Counter sudoku_counter_3: pin names not known
  // Sudoku_Counter sudoku_counter_4: pin names not known; wires that end beside it: N19
  // Big_Hex_Digit_Display big_hex_digit_display_4: pin names not known
  // Sudoku_Counter sudoku_counter_5: pin names not known; wires that end beside it: N28
  // Big_Hex_Digit_Display big_hex_digit_display_5: pin names not known
  // Big_Hex_Digit_Display big_hex_digit_display_6: pin names not known; wires that end beside it: N37
  // Sudoku_Counter sudoku_counter_6: pin names not known
  // Sudoku_Counter sudoku_counter_7: pin names not known; wires that end beside it: N46
  // Big_Hex_Digit_Display big_hex_digit_display_7: pin names not known
  // Big_Hex_Digit_Display big_hex_digit_display_8: pin names not known; wires that end beside it: N55
  // Sudoku_Counter sudoku_counter_8: pin names not known
  // Big_Hex_Digit_Display big_hex_digit_display_9: pin names not known; wires that end beside it: N64, N73
  // Sudoku_Counter sudoku_counter_9: pin names not known
  // Sudoku_Counter sudoku_counter_10: pin names not known
  // Sudoku_Counter sudoku_counter_11: pin names not known
  // Big_Hex_Digit_Display big_hex_digit_display_10: pin names not known
  // Big_Hex_Digit_Display big_hex_digit_display_11: pin names not known
  // Sudoku_Counter sudoku_counter_12: pin names not known; wires that end beside it: N3
  // Big_Hex_Digit_Display big_hex_digit_display_12: pin names not known; wires that end beside it: N2
  // Big_Hex_Digit_Display big_hex_digit_display_13: pin names not known
  // Sudoku_Counter sudoku_counter_13: pin names not known
  // Sudoku_Counter sudoku_counter_14: pin names not known; wires that end beside it: N11
  // Sudoku_Counter sudoku_counter_15: pin names not known; wires that end beside it: N12
  // Big_Hex_Digit_Display big_hex_digit_display_14: pin names not known
  // Big_Hex_Digit_Display big_hex_digit_display_15: pin names not known
  // Sudoku_Counter sudoku_counter_16: pin names not known; wires that end beside it: N20
  // Sudoku_Counter sudoku_counter_17: pin names not known; wires that end beside it: N21
  // Big_Hex_Digit_Display big_hex_digit_display_16: pin names not known
  // Big_Hex_Digit_Display big_hex_digit_display_17: pin names not known
  // Big_Hex_Digit_Display big_hex_digit_display_18: pin names not known; wires that end beside it: N29
  // Sudoku_Counter sudoku_counter_18: pin names not known
  // Sudoku_Counter sudoku_counter_19: pin names not known; wires that end beside it: N30
  // Big_Hex_Digit_Display big_hex_digit_display_19: pin names not known
  // Sudoku_Counter sudoku_counter_20: pin names not known; wires that end beside it: N39
  // Big_Hex_Digit_Display big_hex_digit_display_20: pin names not known; wires that end beside it: N38
  // Big_Hex_Digit_Display big_hex_digit_display_21: pin names not known
  // Sudoku_Counter sudoku_counter_21: pin names not known
  // Sudoku_Counter sudoku_counter_22: pin names not known; wires that end beside it: N47
  // Big_Hex_Digit_Display big_hex_digit_display_22: pin names not known; wires that end beside it: N48
  // Big_Hex_Digit_Display big_hex_digit_display_23: pin names not known
  // Sudoku_Counter sudoku_counter_23: pin names not known
  // Big_Hex_Digit_Display big_hex_digit_display_24: pin names not known; wires that end beside it: N56
  // Sudoku_Counter sudoku_counter_24: pin names not known
  // Sudoku_Counter sudoku_counter_25: pin names not known; wires that end beside it: N57
  // Big_Hex_Digit_Display big_hex_digit_display_25: pin names not known
  // Sudoku_Counter sudoku_counter_26: pin names not known; wires that end beside it: N65, N74
  // Sudoku_Counter sudoku_counter_27: pin names not known; wires that end beside it: N66, N75
  // Big_Hex_Digit_Display big_hex_digit_display_26: pin names not known
  // Big_Hex_Digit_Display big_hex_digit_display_27: pin names not known
  CheckNove checknove_1 (
    .in_1(N1), .in_2(N2), .in_3(N3), .in_4(N4), .in_5(N5), .in_6(N6), .in_7(N7), .in_8(N8), .in_9(N9),
    .out_10(Riga1Err));
  CheckNove checknove_2 (
    .in_1(N1), .in_2(N10), .in_3(N19), .in_4(N28), .in_5(N37), .in_6(N46), .in_7(N55), .in_8(N64),
    .in_9(N73), .out_10(Col1Err));
  CheckNove checknove_3 (
    .in_1(N1), .in_2(N2), .in_3(N3), .in_4(N10), .in_5(N11), .in_6(N12), .in_7(N19), .in_8(N20), .in_9(N21),
    .out_10(Box1Err));
  or or_1 (RigaErr, Riga1Err, Riga2Err, Riga3Err, Riga4Err, Riga5Err, Riga6Err, Riga7Err, Riga8Err, Riga9Err);
  SommaNove sommanove_1 (
    .in_1(N1), .in_2(N2), .in_3(N3), .in_4(N4), .in_5(N5), .in_6(N6), .in_7(N7), .in_8(N8), .in_9(N9),
    .out_10(Riga1Somma));
  // Sudoku_Counter sudoku_counter_28: pin names not known
  // Big_Hex_Digit_Display big_hex_digit_display_28: pin names not known
  // Big_Hex_Digit_Display big_hex_digit_display_29: pin names not known; wires that end beside it: N4
  // Sudoku_Counter sudoku_counter_29: pin names not known
  // Big_Hex_Digit_Display big_hex_digit_display_30: pin names not known; wires that end beside it: N13
  // Sudoku_Counter sudoku_counter_30: pin names not known
  // Sudoku_Counter sudoku_counter_31: pin names not known; wires that end beside it: N22
  // Big_Hex_Digit_Display big_hex_digit_display_31: pin names not known
  // Sudoku_Counter sudoku_counter_32: pin names not known; wires that end beside it: N31
  // Big_Hex_Digit_Display big_hex_digit_display_32: pin names not known
  // Big_Hex_Digit_Display big_hex_digit_display_33: pin names not known; wires that end beside it: N40
  // Sudoku_Counter sudoku_counter_33: pin names not known
  // Sudoku_Counter sudoku_counter_34: pin names not known; wires that end beside it: N49
  // Big_Hex_Digit_Display big_hex_digit_display_34: pin names not known
  // Sudoku_Counter sudoku_counter_35: pin names not known; wires that end beside it: N58
  // Big_Hex_Digit_Display big_hex_digit_display_35: pin names not known
  // Sudoku_Counter sudoku_counter_36: pin names not known; wires that end beside it: N67, N76
  // Big_Hex_Digit_Display big_hex_digit_display_36: pin names not known
  CheckNove checknove_4 (
    .in_1(N10), .in_2(N11), .in_3(N12), .in_4(N13), .in_5(N14), .in_6(N15), .in_7(N16), .in_8(N17),
    .in_9(N18), .out_10(Riga2Err));
  CheckNove checknove_5 (
    .in_1(N2), .in_2(N11), .in_3(N20), .in_4(N29), .in_5(N38), .in_6(N47), .in_7(N56), .in_8(N65),
    .in_9(N74), .out_10(Col2Err));
  CheckNove checknove_6 (
    .in_1(N4), .in_2(N5), .in_3(N6), .in_4(N13), .in_5(N14), .in_6(N15), .in_7(N22), .in_8(N23), .in_9(N24),
    .out_10(Box2Err));
  SommaNove sommanove_2 (
    .in_1(N10), .in_2(N11), .in_3(N12), .in_4(N13), .in_5(N14), .in_6(N15), .in_7(N16), .in_8(N17),
    .in_9(N18), .out_10(Riga2Somma));
  and and_1 (and_1_out, Riga1Somma, Riga2Somma, Riga3Somma, Riga4Somma, Riga5Somma, Riga6Somma, Riga7Somma, Riga8Somma, Riga9Somma);
  // Big_Hex_Digit_Display big_hex_digit_display_37: pin names not known
  // Sudoku_Counter sudoku_counter_37: pin names not known
  // Big_Hex_Digit_Display big_hex_digit_display_38: pin names not known; wires that end beside it: N5
  // Sudoku_Counter sudoku_counter_38: pin names not known
  // Big_Hex_Digit_Display big_hex_digit_display_39: pin names not known; wires that end beside it: N14
  // Sudoku_Counter sudoku_counter_39: pin names not known
  // Sudoku_Counter sudoku_counter_40: pin names not known; wires that end beside it: N23
  // Big_Hex_Digit_Display big_hex_digit_display_40: pin names not known
  // Big_Hex_Digit_Display big_hex_digit_display_41: pin names not known; wires that end beside it: N32
  // Sudoku_Counter sudoku_counter_41: pin names not known
  // Big_Hex_Digit_Display big_hex_digit_display_42: pin names not known; wires that end beside it: N41
  // Sudoku_Counter sudoku_counter_42: pin names not known
  // Sudoku_Counter sudoku_counter_43: pin names not known; wires that end beside it: N50
  // Big_Hex_Digit_Display big_hex_digit_display_43: pin names not known
  // Sudoku_Counter sudoku_counter_44: pin names not known; wires that end beside it: N59
  // Big_Hex_Digit_Display big_hex_digit_display_44: pin names not known
  // Big_Hex_Digit_Display big_hex_digit_display_45: pin names not known; wires that end beside it: N68, N77
  // Sudoku_Counter sudoku_counter_45: pin names not known
  or or_2 (ColErr, Col1Err, Col2Err, Col3Err, Col4Err, Col5Err, Col6Err, Col7Err, Col8Err, Col9Err);
  and and_2 (out_2, and_1_out, ~out_1);  // AND_Gate
  // Sudoku_Counter sudoku_counter_46: pin names not known
  // Big_Hex_Digit_Display big_hex_digit_display_46: pin names not known
  // Sudoku_Counter sudoku_counter_47: pin names not known; wires that end beside it: N6
  // Big_Hex_Digit_Display big_hex_digit_display_47: pin names not known
  // Sudoku_Counter sudoku_counter_48: pin names not known; wires that end beside it: N15
  // Big_Hex_Digit_Display big_hex_digit_display_48: pin names not known
  // Big_Hex_Digit_Display big_hex_digit_display_49: pin names not known; wires that end beside it: N24
  // Sudoku_Counter sudoku_counter_49: pin names not known
  // Sudoku_Counter sudoku_counter_50: pin names not known; wires that end beside it: N33
  // Big_Hex_Digit_Display big_hex_digit_display_50: pin names not known
  // Big_Hex_Digit_Display big_hex_digit_display_51: pin names not known; wires that end beside it: N42
  // Sudoku_Counter sudoku_counter_51: pin names not known
  // Big_Hex_Digit_Display big_hex_digit_display_52: pin names not known; wires that end beside it: N51
  // Sudoku_Counter sudoku_counter_52: pin names not known
  // Big_Hex_Digit_Display big_hex_digit_display_53: pin names not known; wires that end beside it: N60
  // Sudoku_Counter sudoku_counter_53: pin names not known
  // Big_Hex_Digit_Display big_hex_digit_display_54: pin names not known; wires that end beside it: N69, N78
  // Sudoku_Counter sudoku_counter_54: pin names not known
  CheckNove checknove_7 (
    .in_1(N19), .in_2(N20), .in_3(N21), .in_4(N22), .in_5(N23), .in_6(N24), .in_7(N25), .in_8(N26),
    .in_9(N27), .out_10(Riga3Err));
  CheckNove checknove_8 (
    .in_1(N3), .in_2(N12), .in_3(N21), .in_4(N30), .in_5(N39), .in_6(N48), .in_7(N57), .in_8(N66),
    .in_9(N75), .out_10(Col3Err));
  CheckNove checknove_9 (
    .in_1(N7), .in_2(N8), .in_3(N9), .in_4(N16), .in_5(N17), .in_6(N18), .in_7(N25), .in_8(N26), .in_9(N27),
    .out_10(Box3Err));
  SommaNove sommanove_3 (
    .in_1(N19), .in_2(N20), .in_3(N21), .in_4(N22), .in_5(N23), .in_6(N24), .in_7(N25), .in_8(N26),
    .in_9(N27), .out_10(Riga3Somma));
  // Big_Hex_Digit_Display big_hex_digit_display_55: pin names not known
  // Big_Hex_Digit_Display big_hex_digit_display_56: pin names not known
  // Sudoku_Counter sudoku_counter_55: pin names not known
  // Sudoku_Counter sudoku_counter_56: pin names not known
  // Big_Hex_Digit_Display big_hex_digit_display_57: pin names not known; wires that end beside it: N7
  // Sudoku_Counter sudoku_counter_57: pin names not known; wires that end beside it: N8
  // Big_Hex_Digit_Display big_hex_digit_display_58: pin names not known
  // Sudoku_Counter sudoku_counter_58: pin names not known
  // Sudoku_Counter sudoku_counter_59: pin names not known; wires that end beside it: N17
  // Big_Hex_Digit_Display big_hex_digit_display_59: pin names not known; wires that end beside it: N16
  // Sudoku_Counter sudoku_counter_60: pin names not known
  // Big_Hex_Digit_Display big_hex_digit_display_60: pin names not known
  // Sudoku_Counter sudoku_counter_61: pin names not known; wires that end beside it: N26
  // Big_Hex_Digit_Display big_hex_digit_display_61: pin names not known
  // Big_Hex_Digit_Display big_hex_digit_display_62: pin names not known; wires that end beside it: N25
  // Sudoku_Counter sudoku_counter_62: pin names not known
  // Big_Hex_Digit_Display big_hex_digit_display_63: pin names not known; wires that end beside it: N35
  // Sudoku_Counter sudoku_counter_63: pin names not known; wires that end beside it: N34
  // Sudoku_Counter sudoku_counter_64: pin names not known
  // Big_Hex_Digit_Display big_hex_digit_display_64: pin names not known
  // Sudoku_Counter sudoku_counter_65: pin names not known; wires that end beside it: N44
  // Big_Hex_Digit_Display big_hex_digit_display_65: pin names not known
  // Sudoku_Counter sudoku_counter_66: pin names not known; wires that end beside it: N43
  // Big_Hex_Digit_Display big_hex_digit_display_66: pin names not known
  // Sudoku_Counter sudoku_counter_67: pin names not known; wires that end beside it: N52
  // Big_Hex_Digit_Display big_hex_digit_display_67: pin names not known
  // Big_Hex_Digit_Display big_hex_digit_display_68: pin names not known; wires that end beside it: N53
  // Sudoku_Counter sudoku_counter_68: pin names not known
  // Big_Hex_Digit_Display big_hex_digit_display_69: pin names not known; wires that end beside it: N61
  // Sudoku_Counter sudoku_counter_69: pin names not known
  // Sudoku_Counter sudoku_counter_70: pin names not known; wires that end beside it: N62
  // Big_Hex_Digit_Display big_hex_digit_display_70: pin names not known
  // Sudoku_Counter sudoku_counter_71: pin names not known; wires that end beside it: N70, N79
  // Big_Hex_Digit_Display big_hex_digit_display_71: pin names not known; wires that end beside it: N71, N80
  // Sudoku_Counter sudoku_counter_72: pin names not known
  // Big_Hex_Digit_Display big_hex_digit_display_72: pin names not known
  CheckNove checknove_10 (
    .in_1(N28), .in_2(N29), .in_3(N30), .in_4(N31), .in_5(N32), .in_6(N33), .in_7(N34), .in_8(N35),
    .in_9(N36), .out_10(Riga4Err));
  CheckNove checknove_11 (
    .in_1(N4), .in_2(N13), .in_3(N22), .in_4(N31), .in_5(N40), .in_6(N49), .in_7(N58), .in_8(N67),
    .in_9(N76), .out_10(Col4Err));
  CheckNove checknove_12 (
    .in_1(N28), .in_2(N29), .in_3(N30), .in_4(N37), .in_5(N38), .in_6(N39), .in_7(N46), .in_8(N47),
    .in_9(N48), .out_10(Box4Err));
  or or_3 (BoxErr, Box1Err, Box2Err, Box3Err, Box4Err, Box5Err, Box6Err, Box7Err, Box8Err, Box9Err);
  // Sudoku_Counter sudoku_counter_73: pin names not known
  // Big_Hex_Digit_Display big_hex_digit_display_73: pin names not known
  // Sudoku_Counter sudoku_counter_74: pin names not known; wires that end beside it: N9
  // Big_Hex_Digit_Display big_hex_digit_display_74: pin names not known
  // Big_Hex_Digit_Display big_hex_digit_display_75: pin names not known; wires that end beside it: N18
  // Sudoku_Counter sudoku_counter_75: pin names not known
  // Sudoku_Counter sudoku_counter_76: pin names not known; wires that end beside it: N27
  // Big_Hex_Digit_Display big_hex_digit_display_76: pin names not known
  // Big_Hex_Digit_Display big_hex_digit_display_77: pin names not known; wires that end beside it: N36
  // Sudoku_Counter sudoku_counter_77: pin names not known
  // Big_Hex_Digit_Display big_hex_digit_display_78: pin names not known; wires that end beside it: N45
  // Sudoku_Counter sudoku_counter_78: pin names not known
  // Big_Hex_Digit_Display big_hex_digit_display_79: pin names not known; wires that end beside it: N54
  // Sudoku_Counter sudoku_counter_79: pin names not known
  // Sudoku_Counter sudoku_counter_80: pin names not known; wires that end beside it: N63
  // Big_Hex_Digit_Display big_hex_digit_display_80: pin names not known
  // Big_Hex_Digit_Display big_hex_digit_display_81: pin names not known; wires that end beside it: N72, N81
  // Sudoku_Counter sudoku_counter_81: pin names not known
  SommaNove sommanove_4 (
    .in_1(N28), .in_2(N29), .in_3(N30), .in_4(N31), .in_5(N32), .in_6(N33), .in_7(N34), .in_8(N35),
    .in_9(N36), .out_10(Riga4Somma));
  CheckNove checknove_13 (
    .in_1(N37), .in_2(N38), .in_3(N39), .in_4(N40), .in_5(N41), .in_6(N42), .in_7(N43), .in_8(N44),
    .in_9(N45), .out_10(Riga5Err));
  CheckNove checknove_14 (
    .in_1(N5), .in_2(N14), .in_3(N23), .in_4(N32), .in_5(N41), .in_6(N50), .in_7(N59), .in_8(N68),
    .in_9(N77), .out_10(Col5Err));
  CheckNove checknove_15 (
    .in_1(N31), .in_2(N32), .in_3(N33), .in_4(N40), .in_5(N41), .in_6(N42), .in_7(N49), .in_8(N50),
    .in_9(N51), .out_10(Box5Err));
  or or_4 (out_1, RigaErr, ColErr, BoxErr);
  CheckNove checknove_16 (
    .in_1(N46), .in_2(N47), .in_3(N48), .in_4(N49), .in_5(N50), .in_6(N51), .in_7(N52), .in_8(N53),
    .in_9(N54), .out_10(Riga6Err));
  CheckNove checknove_17 (
    .in_1(N6), .in_2(N15), .in_3(N24), .in_4(N33), .in_5(N42), .in_6(N51), .in_7(N60), .in_8(N69),
    .in_9(N78), .out_10(Col6Err));
  CheckNove checknove_18 (
    .in_1(N34), .in_2(N35), .in_3(N36), .in_4(N43), .in_5(N44), .in_6(N45), .in_7(N52), .in_8(N53),
    .in_9(N54), .out_10(Box6Err));
  SommaNove sommanove_5 (
    .in_1(N37), .in_2(N38), .in_3(N39), .in_4(N40), .in_5(N41), .in_6(N42), .in_7(N43), .in_8(N44),
    .in_9(N45), .out_10(Riga5Somma));
  SommaNove sommanove_6 (
    .in_1(N46), .in_2(N47), .in_3(N48), .in_4(N49), .in_5(N50), .in_6(N51), .in_7(N52), .in_8(N53),
    .in_9(N54), .out_10(Riga6Somma));
  CheckNove checknove_19 (
    .in_1(N55), .in_2(N56), .in_3(N57), .in_4(N58), .in_5(N59), .in_6(N60), .in_7(N61), .in_8(N62),
    .in_9(N63), .out_10(Riga7Err));
  CheckNove checknove_20 (
    .in_1(N7), .in_2(N16), .in_3(N25), .in_4(N34), .in_5(N43), .in_6(N52), .in_7(N61), .in_8(N70),
    .in_9(N79), .out_10(Col7Err));
  CheckNove checknove_21 (
    .in_1(N55), .in_2(N56), .in_3(N57), .in_4(N64), .in_5(N65), .in_6(N66), .in_7(N73), .in_8(N74),
    .in_9(N75), .out_10(Box7Err));
  CheckNove checknove_22 (
    .in_1(N64), .in_2(N65), .in_3(N66), .in_4(N67), .in_5(N68), .in_6(N69), .in_7(N70), .in_8(N71),
    .in_9(N72), .out_10(Riga8Err));
  CheckNove checknove_23 (
    .in_1(N8), .in_2(N17), .in_3(N26), .in_4(N35), .in_5(N44), .in_6(N53), .in_7(N62), .in_8(N71),
    .in_9(N80), .out_10(Col8Err));
  CheckNove checknove_24 (
    .in_1(N58), .in_2(N59), .in_3(N60), .in_4(N67), .in_5(N68), .in_6(N69), .in_7(N76), .in_8(N77),
    .in_9(N78), .out_10(Box8Err));
  SommaNove sommanove_7 (
    .in_1(N55), .in_2(N56), .in_3(N57), .in_4(N58), .in_5(N59), .in_6(N60), .in_7(N61), .in_8(N62),
    .in_9(N63), .out_10(Riga7Somma));
  CheckNove checknove_25 (
    .in_1(N73), .in_2(N74), .in_3(N75), .in_4(N76), .in_5(N77), .in_6(N78), .in_7(N79), .in_8(N80),
    .in_9(N81), .out_10(Riga9Err));
  CheckNove checknove_26 (
    .in_1(N9), .in_2(N18), .in_3(N27), .in_4(N36), .in_5(N45), .in_6(N54), .in_7(N63), .in_8(N72),
    .in_9(N81), .out_10(Col9Err));
  CheckNove checknove_27 (
    .in_1(N61), .in_2(N62), .in_3(N63), .in_4(N70), .in_5(N71), .in_6(N72), .in_7(N79), .in_8(N80),
    .in_9(N81), .out_10(Box9Err));
  SommaNove sommanove_8 (
    .in_1(N64), .in_2(N65), .in_3(N66), .in_4(N67), .in_5(N68), .in_6(N69), .in_7(N70), .in_8(N71),
    .in_9(N72), .out_10(Riga8Somma));
  SommaNove sommanove_9 (
    .in_1(N73), .in_2(N74), .in_3(N75), .in_4(N76), .in_5(N77), .in_6(N78), .in_7(N79), .in_8(N80),
    .in_9(N81), .out_10(Riga9Somma));
  Hex_Digit_Display hex_digit_display_1 ();  // open: value, dp
  Hex_Digit_Display hex_digit_display_2 ();  // open: value, dp
  Hex_Digit_Display hex_digit_display_3 ();  // open: value, dp
  Hex_Digit_Display hex_digit_display_4 ();  // open: value, dp
  Hex_Digit_Display hex_digit_display_5 ();  // open: value, dp
  Hex_Digit_Display hex_digit_display_6 ();  // open: value, dp

  // Other names for the same wires on the sheet: Errore = out_1; Vittoria = out_2

  // Notes on the sheet:
  //   Controllo validità
  //   Controllo vittoria
endmodule

module ContatorePlus (
  input  INPUT,
  output [3:0] out_2
);

  wire EqualsZero_out_2;
  wire [3:0] Output;

  Counter #(.width(4), .max('h9)) counter_1 (.Q(Output), .clk(INPUT));  // open: load, D, count, carry, clr
  EqualsZero EqualsZero (.in_1(Output), .out_2(EqualsZero_out_2));
  Multiplexer #(.width(4)) multiplexer_1 (.in0(Output), .out(out_2), .sel(EqualsZero_out_2));  // open: in1, en

  // Notes on the sheet:
  //   Contatore plus
  //   Contatore che conta da 1 a 9, estremi compresi. Al posto di visualizzare 0, manda output indefinito, in modo che il display visualizzi "-".
endmodule

module CheckNove (
  input  [3:0] in_1,
  input  [3:0] in_2,
  input  [3:0] in_3,
  input  [3:0] in_4,
  input  [3:0] in_5,
  input  [3:0] in_6,
  input  [3:0] in_7,
  input  [3:0] in_8,
  input  [3:0] in_9,
  output out_10
);

  wire Out1, Out2, Out3, Out4, Out5, Out6, Out7, Out8, sudoku_comparator_1_p3, sudoku_comparator_2_p3,
       sudoku_comparator_3_p3, sudoku_comparator_4_p3, sudoku_comparator_5_p3, sudoku_comparator_6_p3,
       sudoku_comparator_7_p3, sudoku_comparator_8_p3, sudoku_comparator_9_p3, sudoku_comparator_10_p3,
       sudoku_comparator_11_p3, sudoku_comparator_12_p3, sudoku_comparator_13_p3, sudoku_comparator_14_p3,
       sudoku_comparator_15_p3, sudoku_comparator_16_p3, sudoku_comparator_17_p3, sudoku_comparator_18_p3,
       sudoku_comparator_19_p3, sudoku_comparator_20_p3, sudoku_comparator_21_p3, sudoku_comparator_22_p3,
       sudoku_comparator_23_p3, sudoku_comparator_24_p3, sudoku_comparator_25_p3, sudoku_comparator_26_p3,
       sudoku_comparator_27_p3, sudoku_comparator_28_p3, sudoku_comparator_29_p3, sudoku_comparator_30_p3,
       sudoku_comparator_31_p3, sudoku_comparator_32_p3, sudoku_comparator_33_p3, sudoku_comparator_34_p3,
       sudoku_comparator_35_p3;

  // Sudoku_comparator sudoku_comparator_1: pin names not known; wires that end beside it: in_1, in_4, sudoku_comparator_1_p3
  // Sudoku_comparator sudoku_comparator_2: pin names not known; wires that end beside it: in_1, in_7, sudoku_comparator_2_p3
  // Sudoku_comparator sudoku_comparator_3: pin names not known; wires that end beside it: in_1, in_2, sudoku_comparator_3_p3
  // Sudoku_comparator sudoku_comparator_4: pin names not known; wires that end beside it: in_1, in_5, sudoku_comparator_4_p3
  // Sudoku_comparator sudoku_comparator_5: pin names not known; wires that end beside it: in_1, in_8, sudoku_comparator_5_p3
  // Sudoku_comparator sudoku_comparator_6: pin names not known; wires that end beside it: in_1, in_3, sudoku_comparator_6_p3
  // Sudoku_comparator sudoku_comparator_7: pin names not known; wires that end beside it: in_1, in_6, sudoku_comparator_7_p3
  // Sudoku_comparator sudoku_comparator_8: pin names not known; wires that end beside it: in_1, in_9, sudoku_comparator_8_p3
  or or_1 (Out1, sudoku_comparator_1_p3, sudoku_comparator_2_p3, sudoku_comparator_3_p3, sudoku_comparator_4_p3, sudoku_comparator_5_p3, sudoku_comparator_6_p3, sudoku_comparator_7_p3, sudoku_comparator_8_p3);
  // Sudoku_comparator sudoku_comparator_9: pin names not known; wires that end beside it: in_4, in_7, sudoku_comparator_9_p3
  // Sudoku_comparator sudoku_comparator_10: pin names not known; wires that end beside it: in_4, in_2, sudoku_comparator_10_p3
  // Sudoku_comparator sudoku_comparator_11: pin names not known; wires that end beside it: in_4, in_5, sudoku_comparator_11_p3
  // Sudoku_comparator sudoku_comparator_12: pin names not known; wires that end beside it: in_4, in_8, sudoku_comparator_12_p3
  // Sudoku_comparator sudoku_comparator_13: pin names not known; wires that end beside it: in_4, in_3, sudoku_comparator_13_p3
  // Sudoku_comparator sudoku_comparator_14: pin names not known; wires that end beside it: in_4, in_6, sudoku_comparator_14_p3
  // Sudoku_comparator sudoku_comparator_15: pin names not known; wires that end beside it: in_4, in_9, sudoku_comparator_15_p3
  or or_2 (out_10, Out1, Out2, Out3, Out4, Out5, Out6, Out7, Out8);
  or or_3 (Out2, sudoku_comparator_9_p3, sudoku_comparator_10_p3, sudoku_comparator_11_p3, sudoku_comparator_12_p3, sudoku_comparator_13_p3, sudoku_comparator_14_p3, sudoku_comparator_15_p3);
  // Sudoku_comparator sudoku_comparator_16: pin names not known; wires that end beside it: in_7, in_2, sudoku_comparator_16_p3
  // Sudoku_comparator sudoku_comparator_17: pin names not known; wires that end beside it: in_7, in_5, sudoku_comparator_17_p3
  // Sudoku_comparator sudoku_comparator_18: pin names not known; wires that end beside it: in_7, in_8, sudoku_comparator_18_p3
  // Sudoku_comparator sudoku_comparator_19: pin names not known; wires that end beside it: in_7, in_3, sudoku_comparator_19_p3
  // Sudoku_comparator sudoku_comparator_20: pin names not known; wires that end beside it: in_7, in_6, sudoku_comparator_20_p3
  // Sudoku_comparator sudoku_comparator_21: pin names not known; wires that end beside it: in_7, in_9, sudoku_comparator_21_p3
  or or_4 (Out3, sudoku_comparator_16_p3, sudoku_comparator_17_p3, sudoku_comparator_18_p3, sudoku_comparator_19_p3, sudoku_comparator_20_p3, sudoku_comparator_21_p3);
  // Sudoku_comparator sudoku_comparator_22: pin names not known; wires that end beside it: in_2, in_5, sudoku_comparator_22_p3
  // Sudoku_comparator sudoku_comparator_23: pin names not known; wires that end beside it: in_2, in_8, sudoku_comparator_23_p3
  // Sudoku_comparator sudoku_comparator_24: pin names not known; wires that end beside it: in_2, in_3, sudoku_comparator_24_p3
  // Sudoku_comparator sudoku_comparator_25: pin names not known; wires that end beside it: in_2, in_6, sudoku_comparator_25_p3
  // Sudoku_comparator sudoku_comparator_26: pin names not known; wires that end beside it: in_2, in_9, sudoku_comparator_26_p3
  or or_5 (Out4, sudoku_comparator_22_p3, sudoku_comparator_23_p3, sudoku_comparator_24_p3, sudoku_comparator_25_p3, sudoku_comparator_26_p3);
  // Sudoku_comparator sudoku_comparator_27: pin names not known; wires that end beside it: in_5, in_8, sudoku_comparator_27_p3
  // Sudoku_comparator sudoku_comparator_28: pin names not known; wires that end beside it: in_5, in_3, sudoku_comparator_28_p3
  // Sudoku_comparator sudoku_comparator_29: pin names not known; wires that end beside it: in_5, in_6, sudoku_comparator_29_p3
  // Sudoku_comparator sudoku_comparator_30: pin names not known; wires that end beside it: in_5, in_9, sudoku_comparator_30_p3
  or or_6 (Out5, sudoku_comparator_27_p3, sudoku_comparator_28_p3, sudoku_comparator_29_p3, sudoku_comparator_30_p3);
  // Sudoku_comparator sudoku_comparator_31: pin names not known; wires that end beside it: in_8, in_3, sudoku_comparator_31_p3
  // Sudoku_comparator sudoku_comparator_32: pin names not known; wires that end beside it: in_8, in_6, sudoku_comparator_32_p3
  // Sudoku_comparator sudoku_comparator_33: pin names not known; wires that end beside it: in_8, in_9, sudoku_comparator_33_p3
  or or_7 (Out6, sudoku_comparator_31_p3, sudoku_comparator_32_p3, sudoku_comparator_33_p3);
  // Sudoku_comparator sudoku_comparator_34: pin names not known; wires that end beside it: in_3, in_6, sudoku_comparator_34_p3
  // Sudoku_comparator sudoku_comparator_35: pin names not known; wires that end beside it: in_3, in_9, sudoku_comparator_35_p3
  or or_8 (Out7, sudoku_comparator_34_p3, sudoku_comparator_35_p3);
  // Sudoku_comparator sudoku_comparator_36: pin names not known; wires that end beside it: in_6, in_9, Out8

  // Other names for the same wires on the sheet: N1[3:0] = in_1; N2[3:0] = in_4; N3[3:0] = in_7; N4[3:0] = in_2;
  //   N5[3:0] = in_5; N6[3:0] = in_8; N7[3:0] = in_3; N8[3:0] = in_6; N9[3:0] = in_9

  // Notes on the sheet:
  //   CheckNove
  //   Funzione che prende in input 9 numeri e controlla se almeno due di loro sono uguali fra loro.
  //   L'input non definito (nel display, "-") non è considerato uguale a nessun altro input, nemmeno a se stesso.
endmodule

module SuperComparator (
  input  [3:0] in_1,
  input  [3:0] in_2,
  output out_3
);

  wire B0, B1, B2, B3, clock_1_out, Equal, EqualsZero_out_2, multiplexer_1_out, xor_1_out, xor_2_out,
       xor_3_out, xor_4_out;
  wire [3:0] A;

  FilteredInput4 filteredinput4_1 (.in_1(in_1), .out_2(A));
  xor xor_1 (xor_1_out, A[0], B0);
  xor xor_2 (xor_2_out, A[1], B1);
  xor xor_3 (xor_3_out, A[2], B2);
  xor xor_4 (xor_4_out, A[3], B3);
  nor nor_1 (Equal, xor_1_out, xor_2_out, xor_3_out, xor_4_out);
  FilteredInput4 filteredinput4_2 (.in_1(in_2), .out_2({B3, B2, B1, B0}));
  Multiplexer multiplexer_1 (.in0(Equal), .in1(1'b0), .out(multiplexer_1_out), .sel(EqualsZero_out_2));  // open: en
  EqualsZero EqualsZero (.in_1(A), .out_2(EqualsZero_out_2));
  Clock clock_1 (.out(clock_1_out));
  D_Flip_Flop d_ff_1 (.clk(clock_1_out), .D(multiplexer_1_out), .Q(out_3));  // open: Qn, preset, en, reset

  // Notes on the sheet:
  //   Sudoku comparator
  //   Comparatore a 4 bit modificato per il gioco del sudoku.
  //   Un input non definito (display "-") viene interpretato come 0, e due 0 NON sono considerati uguali (possono esserci più celle vuote nel gioco)
endmodule

module FilteredInput (
  input  in_1,
  output out_2
);

  Multiplexer multiplexer_1 (.in0(in_1), .out(out_2), .sel(1'b0));  // open: in1, en
  Pull_Resistor pull_resistor_1 (.node(out_2));

  // Notes on the sheet:
  //   Input Filter
  //   Funzione che non fa altro che propagare l'input, con l'accortezza di modificare x (indefinito) in 0.
  //   Necessario dato che applicare un pull resistor direttamente all'input andrebbe a modificare il valore del cavo stesso, per esempio impostando il display a "0" invece di "-".
endmodule

module FilteredInput4 (
  input  [3:0] in_1,
  output [3:0] out_2
);

  FilteredInput filteredinput_1 (.in_1(in_1[0]), .out_2(out_2[0]));
  FilteredInput filteredinput_2 (.in_1(in_1[1]), .out_2(out_2[1]));
  FilteredInput filteredinput_3 (.in_1(in_1[2]), .out_2(out_2[2]));
  FilteredInput filteredinput_4 (.in_1(in_1[3]), .out_2(out_2[3]));

  // Notes on the sheet:
  //   Input Filter 4
  //   Versione a 4 bit di Input Filter.
endmodule

module EqualsZero (
  input  [3:0] in_1,
  output out_2
);

  wire xor_1_out, xor_2_out, xor_3_out, xor_4_out;

  xor xor_1 (xor_1_out, in_1[0], 1'b0);
  xor xor_2 (xor_2_out, in_1[1], 1'b0);
  xor xor_3 (xor_3_out, in_1[2], 1'b0);
  xor xor_4 (xor_4_out, in_1[3], 1'b0);
  nor nor_1 (out_2, xor_1_out, xor_2_out, xor_3_out, xor_4_out);

  // Other names for the same wires on the sheet: A0 = in_1[0]; A1 = in_1[1]; A2 = in_1[2]; A3 = in_1[3]

  // Notes on the sheet:
  //   Equals 0
  //   Funzione che verifica se il numero a 4 bit in input è zero. Più efficente di un comparatore normale.
endmodule

module VecchiaGriglia (
);

  wire B1, B2, B3, B4, B5, B6, B7, B8, B9, B10, B11, B12, B13, B14, B15, B16, B17, B18, B19, B20, B21, B22,
       B23, B24, B25, B26, B27, B28, B29, B30, B31, B32, B33, B34, B35, B36, B37, B38, B39, B40, B41, B42,
       B43, B44, B45, B46, B47, B48, B49, B50, B51, B52, B53, B54, B55, B56, B57, B58, B59, B60, B61, B62,
       B63, B64, B65, B66, B67, B68, B69, B70, B71, B72, B73, B74, B75, B76, B77, B78, B79, B80, B81;
  wire [3:0] N1, N2, N3, N4, N5, N6, N7, N8, N9, N10, N11, N12, N13, N14, N15, N16, N17, N18, N19, N20, N21,
       N22, N23, N24, N25, N26, N27, N28, N29, N30, N31, N32, N33, N34, N35, N36, N37, N38, N39, N40, N41,
       N42, N43, N44, N45, N46, N47, N48, N49, N50, N51, N52, N53, N54, N55, N56, N57, N58, N59, N60, N61,
       N62, N63, N64, N65, N66, N67, N68, N69, N70, N71, N72, N73, N74, N75, N76, N77, N78, N79, N80, N81;

  Button button_1 (.out(B1));
  Hex_Digit_Display hex_digit_display_1 (.value(N1));  // open: dp
  Button button_2 (.out(B10));
  Hex_Digit_Display hex_digit_display_2 (.value(N10));  // open: dp
  Button button_3 (.out(B19));
  Hex_Digit_Display hex_digit_display_3 (.value(N19));  // open: dp
  Button button_4 (.out(B28));
  Hex_Digit_Display hex_digit_display_4 (.value(N28));  // open: dp
  Button button_5 (.out(B37));
  Hex_Digit_Display hex_digit_display_5 (.value(N37));  // open: dp
  Button button_6 (.out(B46));
  Hex_Digit_Display hex_digit_display_6 (.value(N46));  // open: dp
  Button button_7 (.out(B55));
  Hex_Digit_Display hex_digit_display_7 (.value(N55));  // open: dp
  Button button_8 (.out(B64));
  Hex_Digit_Display hex_digit_display_8 (.value(N64));  // open: dp
  Button button_9 (.out(B73));
  Hex_Digit_Display hex_digit_display_9 (.value(N73));  // open: dp
  Button button_10 (.out(B3));
  Button button_11 (.out(B2));
  Hex_Digit_Display hex_digit_display_10 (.value(N3));  // open: dp
  Hex_Digit_Display hex_digit_display_11 (.value(N2));  // open: dp
  Button button_12 (.out(B12));
  Button button_13 (.out(B11));
  Hex_Digit_Display hex_digit_display_12 (.value(N11));  // open: dp
  Hex_Digit_Display hex_digit_display_13 (.value(N12));  // open: dp
  Button button_14 (.out(B21));
  Button button_15 (.out(B20));
  Hex_Digit_Display hex_digit_display_14 (.value(N21));  // open: dp
  Hex_Digit_Display hex_digit_display_15 (.value(N20));  // open: dp
  Button button_16 (.out(B30));
  Button button_17 (.out(B29));
  Hex_Digit_Display hex_digit_display_16 (.value(N30));  // open: dp
  Hex_Digit_Display hex_digit_display_17 (.value(N29));  // open: dp
  Button button_18 (.out(B38));
  Button button_19 (.out(B39));
  Hex_Digit_Display hex_digit_display_18 (.value(N39));  // open: dp
  Hex_Digit_Display hex_digit_display_19 (.value(N38));  // open: dp
  Button button_20 (.out(B48));
  Button button_21 (.out(B47));
  Hex_Digit_Display hex_digit_display_20 (.value(N47));  // open: dp
  Hex_Digit_Display hex_digit_display_21 (.value(N48));  // open: dp
  Button button_22 (.out(B56));
  Button button_23 (.out(B57));
  Hex_Digit_Display hex_digit_display_22 (.value(N56));  // open: dp
  Hex_Digit_Display hex_digit_display_23 (.value(N57));  // open: dp
  Button button_24 (.out(B65));
  Button button_25 (.out(B66));
  Hex_Digit_Display hex_digit_display_24 (.value(N66));  // open: dp
  Hex_Digit_Display hex_digit_display_25 (.value(N65));  // open: dp
  Button button_26 (.out(B75));
  Button button_27 (.out(B74));
  Hex_Digit_Display hex_digit_display_26 (.value(N74));  // open: dp
  Hex_Digit_Display hex_digit_display_27 (.value(N75));  // open: dp
  ContatorePlus contatoreplus_1 (.out_2(N2), .INPUT(B2));
  ContatorePlus contatoreplus_2 (.out_2(N1), .INPUT(B1));
  ContatorePlus contatoreplus_3 (.out_2(N11), .INPUT(B11));
  ContatorePlus contatoreplus_4 (.out_2(N10), .INPUT(B10));
  ContatorePlus contatoreplus_5 (.out_2(N20), .INPUT(B20));
  ContatorePlus contatoreplus_6 (.out_2(N19), .INPUT(B19));
  ContatorePlus contatoreplus_7 (.out_2(N29), .INPUT(B29));
  ContatorePlus contatoreplus_8 (.out_2(N28), .INPUT(B28));
  ContatorePlus contatoreplus_9 (.out_2(N38), .INPUT(B38));
  ContatorePlus contatoreplus_10 (.out_2(N37), .INPUT(B37));
  ContatorePlus contatoreplus_11 (.out_2(N46), .INPUT(B46));
  ContatorePlus contatoreplus_12 (.out_2(N47), .INPUT(B47));
  ContatorePlus contatoreplus_13 (.out_2(N56), .INPUT(B56));
  ContatorePlus contatoreplus_14 (.out_2(N55), .INPUT(B55));
  ContatorePlus contatoreplus_15 (.out_2(N64), .INPUT(B64));
  ContatorePlus contatoreplus_16 (.out_2(N65), .INPUT(B65));
  ContatorePlus contatoreplus_17 (.out_2(N74), .INPUT(B74));
  ContatorePlus contatoreplus_18 (.out_2(N73), .INPUT(B73));
  Button button_28 (.out(B5));
  Button button_29 (.out(B4));
  Hex_Digit_Display hex_digit_display_28 (.value(N5));  // open: dp
  Hex_Digit_Display hex_digit_display_29 (.value(N4));  // open: dp
  Button button_30 (.out(B13));
  Button button_31 (.out(B14));
  Hex_Digit_Display hex_digit_display_30 (.value(N14));  // open: dp
  Hex_Digit_Display hex_digit_display_31 (.value(N13));  // open: dp
  Button button_32 (.out(B23));
  Button button_33 (.out(B22));
  Hex_Digit_Display hex_digit_display_32 (.value(N22));  // open: dp
  Hex_Digit_Display hex_digit_display_33 (.value(N23));  // open: dp
  Button button_34 (.out(B31));
  Button button_35 (.out(B32));
  Hex_Digit_Display hex_digit_display_34 (.value(N32));  // open: dp
  Hex_Digit_Display hex_digit_display_35 (.value(N31));  // open: dp
  Button button_36 (.out(B40));
  Button button_37 (.out(B41));
  Hex_Digit_Display hex_digit_display_36 (.value(N40));  // open: dp
  Hex_Digit_Display hex_digit_display_37 (.value(N41));  // open: dp
  Button button_38 (.out(B49));
  Button button_39 (.out(B50));
  Hex_Digit_Display hex_digit_display_38 (.value(N49));  // open: dp
  Hex_Digit_Display hex_digit_display_39 (.value(N50));  // open: dp
  Button button_40 (.out(B59));
  Button button_41 (.out(B58));
  Hex_Digit_Display hex_digit_display_40 (.value(N58));  // open: dp
  Hex_Digit_Display hex_digit_display_41 (.value(N59));  // open: dp
  Button button_42 (.out(B67));
  Button button_43 (.out(B68));
  Hex_Digit_Display hex_digit_display_42 (.value(N68));  // open: dp
  Hex_Digit_Display hex_digit_display_43 (.value(N67));  // open: dp
  Button button_44 (.out(B76));
  Button button_45 (.out(B77));
  Hex_Digit_Display hex_digit_display_44 (.value(N76));  // open: dp
  Hex_Digit_Display hex_digit_display_45 (.value(N77));  // open: dp
  ContatorePlus contatoreplus_19 (.out_2(N3), .INPUT(B3));
  ContatorePlus contatoreplus_20 (.out_2(N12), .INPUT(B12));
  ContatorePlus contatoreplus_21 (.out_2(N21), .INPUT(B21));
  ContatorePlus contatoreplus_22 (.out_2(N30), .INPUT(B30));
  ContatorePlus contatoreplus_23 (.out_2(N39), .INPUT(B39));
  ContatorePlus contatoreplus_24 (.out_2(N48), .INPUT(B48));
  ContatorePlus contatoreplus_25 (.out_2(N57), .INPUT(B57));
  ContatorePlus contatoreplus_26 (.out_2(N66), .INPUT(B66));
  ContatorePlus contatoreplus_27 (.out_2(N75), .INPUT(B75));
  Button button_46 (.out(B6));
  Button button_47 (.out(B7));
  Hex_Digit_Display hex_digit_display_46 (.value(N7));  // open: dp
  Hex_Digit_Display hex_digit_display_47 (.value(N6));  // open: dp
  Button button_48 (.out(B16));
  Button button_49 (.out(B15));
  Hex_Digit_Display hex_digit_display_48 (.value(N15));  // open: dp
  Hex_Digit_Display hex_digit_display_49 (.value(N16));  // open: dp
  Button button_50 (.out(B24));
  Button button_51 (.out(B25));
  Hex_Digit_Display hex_digit_display_50 (.value(N25));  // open: dp
  Hex_Digit_Display hex_digit_display_51 (.value(N24));  // open: dp
  Button button_52 (.out(B34));
  Button button_53 (.out(B33));
  Hex_Digit_Display hex_digit_display_52 (.value(N34));  // open: dp
  Hex_Digit_Display hex_digit_display_53 (.value(N33));  // open: dp
  Button button_54 (.out(B43));
  Button button_55 (.out(B42));
  Hex_Digit_Display hex_digit_display_54 (.value(N43));  // open: dp
  Hex_Digit_Display hex_digit_display_55 (.value(N42));  // open: dp
  Button button_56 (.out(B51));
  Button button_57 (.out(B52));
  Hex_Digit_Display hex_digit_display_56 (.value(N51));  // open: dp
  Hex_Digit_Display hex_digit_display_57 (.value(N52));  // open: dp
  Button button_58 (.out(B61));
  Button button_59 (.out(B60));
  Hex_Digit_Display hex_digit_display_58 (.value(N61));  // open: dp
  Hex_Digit_Display hex_digit_display_59 (.value(N60));  // open: dp
  Button button_60 (.out(B70));
  Button button_61 (.out(B69));
  Hex_Digit_Display hex_digit_display_60 (.value(N70));  // open: dp
  Hex_Digit_Display hex_digit_display_61 (.value(N69));  // open: dp
  Button button_62 (.out(B79));
  Button button_63 (.out(B78));
  Hex_Digit_Display hex_digit_display_62 (.value(N78));  // open: dp
  Hex_Digit_Display hex_digit_display_63 (.value(N79));  // open: dp
  ContatorePlus contatoreplus_28 (.out_2(N4), .INPUT(B4));
  ContatorePlus contatoreplus_29 (.out_2(N13), .INPUT(B13));
  ContatorePlus contatoreplus_30 (.out_2(N22), .INPUT(B22));
  ContatorePlus contatoreplus_31 (.out_2(N31), .INPUT(B31));
  ContatorePlus contatoreplus_32 (.out_2(N40), .INPUT(B40));
  ContatorePlus contatoreplus_33 (.out_2(N49), .INPUT(B49));
  ContatorePlus contatoreplus_34 (.out_2(N58), .INPUT(B58));
  ContatorePlus contatoreplus_35 (.out_2(N67), .INPUT(B67));
  ContatorePlus contatoreplus_36 (.out_2(N76), .INPUT(B76));
  Button button_64 (.out(B9));
  Button button_65 (.out(B8));
  Hex_Digit_Display hex_digit_display_64 (.value(N9));  // open: dp
  Hex_Digit_Display hex_digit_display_65 (.value(N8));  // open: dp
  Button button_66 (.out(B17));
  Button button_67 (.out(B18));
  Hex_Digit_Display hex_digit_display_66 (.value(N17));  // open: dp
  Hex_Digit_Display hex_digit_display_67 (.value(N18));  // open: dp
  Button button_68 (.out(B27));
  Button button_69 (.out(B26));
  Hex_Digit_Display hex_digit_display_68 (.value(N27));  // open: dp
  Hex_Digit_Display hex_digit_display_69 (.value(N26));  // open: dp
  Button button_70 (.out(B36));
  Button button_71 (.out(B35));
  Hex_Digit_Display hex_digit_display_70 (.value(N35));  // open: dp
  Hex_Digit_Display hex_digit_display_71 (.value(N36));  // open: dp
  Button button_72 (.out(B45));
  Button button_73 (.out(B44));
  Hex_Digit_Display hex_digit_display_72 (.value(N44));  // open: dp
  Hex_Digit_Display hex_digit_display_73 (.value(N45));  // open: dp
  Button button_74 (.out(B54));
  Button button_75 (.out(B53));
  Hex_Digit_Display hex_digit_display_74 (.value(N54));  // open: dp
  Hex_Digit_Display hex_digit_display_75 (.value(N53));  // open: dp
  Button button_76 (.out(B63));
  Button button_77 (.out(B62));
  Hex_Digit_Display hex_digit_display_76 (.value(N63));  // open: dp
  Hex_Digit_Display hex_digit_display_77 (.value(N62));  // open: dp
  Button button_78 (.out(B72));
  Button button_79 (.out(B71));
  Hex_Digit_Display hex_digit_display_78 (.value(N72));  // open: dp
  Hex_Digit_Display hex_digit_display_79 (.value(N71));  // open: dp
  Button button_80 (.out(B81));
  Button button_81 (.out(B80));
  Hex_Digit_Display hex_digit_display_80 (.value(N80));  // open: dp
  Hex_Digit_Display hex_digit_display_81 (.value(N81));  // open: dp
  ContatorePlus contatoreplus_37 (.out_2(N6), .INPUT(B6));
  ContatorePlus contatoreplus_38 (.out_2(N5), .INPUT(B5));
  ContatorePlus contatoreplus_39 (.out_2(N14), .INPUT(B14));
  ContatorePlus contatoreplus_40 (.out_2(N15), .INPUT(B15));
  ContatorePlus contatoreplus_41 (.out_2(N24), .INPUT(B24));
  ContatorePlus contatoreplus_42 (.out_2(N23), .INPUT(B23));
  ContatorePlus contatoreplus_43 (.out_2(N33), .INPUT(B33));
  ContatorePlus contatoreplus_44 (.out_2(N32), .INPUT(B32));
  ContatorePlus contatoreplus_45 (.out_2(N41), .INPUT(B41));
  ContatorePlus contatoreplus_46 (.out_2(N42), .INPUT(B42));
  ContatorePlus contatoreplus_47 (.out_2(N51), .INPUT(B51));
  ContatorePlus contatoreplus_48 (.out_2(N50), .INPUT(B50));
  ContatorePlus contatoreplus_49 (.out_2(N60), .INPUT(B60));
  ContatorePlus contatoreplus_50 (.out_2(N59), .INPUT(B59));
  ContatorePlus contatoreplus_51 (.out_2(N69), .INPUT(B69));
  ContatorePlus contatoreplus_52 (.out_2(N68), .INPUT(B68));
  ContatorePlus contatoreplus_53 (.out_2(N77), .INPUT(B77));
  ContatorePlus contatoreplus_54 (.out_2(N78), .INPUT(B78));
  ContatorePlus contatoreplus_55 (.out_2(N7), .INPUT(B7));
  ContatorePlus contatoreplus_56 (.out_2(N16), .INPUT(B16));
  ContatorePlus contatoreplus_57 (.out_2(N25), .INPUT(B25));
  ContatorePlus contatoreplus_58 (.out_2(N34), .INPUT(B34));
  ContatorePlus contatoreplus_59 (.out_2(N43), .INPUT(B43));
  ContatorePlus contatoreplus_60 (.out_2(N52), .INPUT(B52));
  ContatorePlus contatoreplus_61 (.out_2(N61), .INPUT(B61));
  ContatorePlus contatoreplus_62 (.out_2(N70), .INPUT(B70));
  ContatorePlus contatoreplus_63 (.out_2(N79), .INPUT(B79));
  ContatorePlus contatoreplus_64 (.out_2(N8), .INPUT(B8));
  ContatorePlus contatoreplus_65 (.out_2(N17), .INPUT(B17));
  ContatorePlus contatoreplus_66 (.out_2(N26), .INPUT(B26));
  ContatorePlus contatoreplus_67 (.out_2(N35), .INPUT(B35));
  ContatorePlus contatoreplus_68 (.out_2(N44), .INPUT(B44));
  ContatorePlus contatoreplus_69 (.out_2(N53), .INPUT(B53));
  ContatorePlus contatoreplus_70 (.out_2(N62), .INPUT(B62));
  ContatorePlus contatoreplus_71 (.out_2(N71), .INPUT(B71));
  ContatorePlus contatoreplus_72 (.out_2(N80), .INPUT(B80));
  ContatorePlus contatoreplus_73 (.out_2(N9), .INPUT(B9));
  ContatorePlus contatoreplus_74 (.out_2(N18), .INPUT(B18));
  ContatorePlus contatoreplus_75 (.out_2(N27), .INPUT(B27));
  ContatorePlus contatoreplus_76 (.out_2(N36), .INPUT(B36));
  ContatorePlus contatoreplus_77 (.out_2(N45), .INPUT(B45));
  ContatorePlus contatoreplus_78 (.out_2(N54), .INPUT(B54));
  ContatorePlus contatoreplus_79 (.out_2(N63), .INPUT(B63));
  ContatorePlus contatoreplus_80 (.out_2(N72), .INPUT(B72));
  ContatorePlus contatoreplus_81 (.out_2(N81), .INPUT(B81));

  // Notes on the sheet:
  //   Vecchia Griglia
  //   Display touch
  //   Questo circuito di fatto non fa piu parte del progetto. Si tratta della vecchia versione della griglia sudoku, che usava il display standard e dei pulsanti per cambiare le cifre
endmodule

module SommaNove (
  input  [3:0] in_1,
  input  [3:0] in_2,
  input  [3:0] in_3,
  input  [3:0] in_4,
  input  [3:0] in_5,
  input  [3:0] in_6,
  input  [3:0] in_7,
  input  [3:0] in_8,
  input  [3:0] in_9,
  output out_10
);

  wire [5:0] adder_1_out, adder_2_out, adder_3_out, adder_4_out, adder_5_out, adder_6_out, adder_7_out,
       adder_8_out, bit_extender_1_out, bit_extender_2_out, bit_extender_3_out, bit_extender_4_out,
       bit_extender_5_out, bit_extender_6_out, bit_extender_7_out, bit_extender_8_out, bit_extender_9_out;

  assign bit_extender_1_out = {{2{1'b0}}, in_1};  // Bit_Extender bit_extender_1
  Adder #(.width(6)) adder_1 (.a(bit_extender_1_out), .b(bit_extender_2_out), .out(adder_1_out));  // open: cin, cout
  assign bit_extender_2_out = {{2{1'b0}}, in_4};  // Bit_Extender bit_extender_2
  assign bit_extender_3_out = {{2{1'b0}}, in_7};  // Bit_Extender bit_extender_3
  Adder #(.width(6)) adder_2 (.a(bit_extender_3_out), .b(bit_extender_4_out), .out(adder_2_out));  // open: cin, cout
  assign bit_extender_4_out = {{2{1'b0}}, in_2};  // Bit_Extender bit_extender_4
  assign bit_extender_5_out = {{2{1'b0}}, in_5};  // Bit_Extender bit_extender_5
  Adder #(.width(6)) adder_3 (.a(bit_extender_5_out), .b(bit_extender_6_out), .out(adder_3_out));  // open: cin, cout
  assign bit_extender_6_out = {{2{1'b0}}, in_8};  // Bit_Extender bit_extender_6
  assign bit_extender_7_out = {{2{1'b0}}, in_3};  // Bit_Extender bit_extender_7
  Adder #(.width(6)) adder_4 (.a(bit_extender_7_out), .b(bit_extender_8_out), .out(adder_4_out));  // open: cin, cout
  assign bit_extender_8_out = {{2{1'b0}}, in_6};  // Bit_Extender bit_extender_8
  Adder #(.width(6)) adder_5 (.a(adder_1_out), .b(adder_2_out), .out(adder_5_out));  // open: cin, cout
  Adder #(.width(6)) adder_6 (.a(adder_3_out), .b(adder_4_out), .out(adder_6_out));  // open: cin, cout
  Adder #(.width(6)) adder_7 (.a(adder_5_out), .b(adder_6_out), .out(adder_7_out));  // open: cin, cout
  assign bit_extender_9_out = {{2{1'b0}}, in_9};  // Bit_Extender bit_extender_9
  Adder #(.width(6)) adder_8 (.a(adder_7_out), .b(bit_extender_9_out), .out(adder_8_out));  // open: cin, cout
  // Sudoku_comparator sudoku_comparator_1: pin names not known; wires that end beside it: adder_8_out, 6'b101101, out_10

  // Other names for the same wires on the sheet: N1[3:0] = in_1; N2[3:0] = in_4; N3[3:0] = in_7; N4[3:0] = in_2;
  //   N5[3:0] = in_5; N6[3:0] = in_8; N7[3:0] = in_3; N8[3:0] = in_6; N9[3:0] = in_9

  // Notes on the sheet:
  //   SommaNove
  //   Funzione che prende in input 9 numeri (bitwidth 4) e verifica se la loro somma e' uguale a 45 (2d), ovvero 1+2+3+4+5+6+7+8+9
endmodule
